# Fritzing sketch alu (saved by Fritzing 0.9.3b)
breadboards: 3

parts:
  IC11 = DIP - 24 pins [chip_label=74LS181 package="DIP (Dual Inline) [THT]"]
  IC12 = DIP - 24 pins [chip_label=74LS181 package="DIP (Dual Inline) [THT]"]
  BUS = female pin header, 8 pins [form="♀ (female)"]
  RESULT = female pin header, 8 pins [form="♀ (female)"]
  B_REGISTER = female pin header, 8 pins [form="♀ (female)"]
  IC13 = IC, DIP package, 14 pins [chip_label=74HCT00]
  IC16 = IC, DIP package, 16 pins [chip_label=74HCT173]
  CARRY/BORROW_IN = female pin header, 2 pins [form="♀ (female)"]
  LED2 = LED - 5mm [color="Yellow (585nm)" package="5 mm [THT]"]
  LED3 = LED - 5mm [color="Yellow (585nm)" package="5 mm [THT]"]
  LED4 = LED - 5mm [color="Yellow (585nm)" package="5 mm [THT]"]
  LED5 = LED - 5mm [color="Yellow (585nm)" package="5 mm [THT]"]
  R1 = Resistor [tolerance=±5% resistance=220 package=THT]
  R2 = Resistor [tolerance=±5% resistance=220 package=THT]
  R3 = Resistor [tolerance=±5% resistance=220 package=THT]
  R4 = Resistor [tolerance=±5% resistance=220 package=THT]
  IC17 = DIP - 14 pins [chip_label=74HCT04 package="DIP (Dual Inline) [THT]"]
  RESULT_2 = female pin header, 8 pins [form="♀ (female)"]
  LED9 = LED - 5mm [color="Red (633nm)" package="5 mm [THT]"]
  LED10 = LED - 5mm [color="Red (633nm)" package="5 mm [THT]"]
  LED11 = LED - 5mm [color="Red (633nm)" package="5 mm [THT]"]
  LED12 = LED - 5mm [color="Red (633nm)" package="5 mm [THT]"]
  LED13 = LED - 5mm [color="Red (633nm)" package="5 mm [THT]"]
  LED14 = LED - 5mm [color="Red (633nm)" package="5 mm [THT]"]
  LED15 = LED - 5mm [color="Red (633nm)" package="5 mm [THT]"]
  LED16 = LED - 5mm [color="Red (633nm)" package="5 mm [THT]"]
  R5 = Resistor [tolerance=±5% resistance=220 package=THT]
  R6 = Resistor [tolerance=±5% resistance=220 package=THT]
  R8 = Resistor [tolerance=±5% resistance=220 package=THT]
  R9 = Resistor [tolerance=±5% resistance=220 package=THT]
  R10 = Resistor [tolerance=±5% resistance=220 package=THT]
  R11 = Resistor [tolerance=±5% resistance=220 package=THT]
  R13 = Resistor [tolerance=±5% resistance=220 package=THT]
  R14 = Resistor [tolerance=±5% resistance=220 package=THT]
  R15 = Resistor [tolerance=±5% resistance=220 package=THT]
  R16 = Resistor [tolerance=±5% resistance=220 package=THT]
  LED17 = LED - 5mm [color="Yellow (585nm)" package="5 mm [THT]"]
  LED18 = LED - 5mm [color="Yellow (585nm)" package="5 mm [THT]"]
  LED19 = LED - 5mm [color="Yellow (585nm)" package="5 mm [THT]"]
  LED20 = LED - 5mm [color="Yellow (585nm)" package="5 mm [THT]"]
  FLAGS_IN = female pin header, 2 pins [form="♀ (female)"]
  IC20 = 74HCT245 [chip_label=74HCT245 package="DIP (Dual Inline) [THT]"]
  IC21 = 74HCT377 [chip_label=74HCT377 package="DIP (Dual Inline) [THT]"]
  IC22 = DIP - 14 pins [chip_label=74HCT04 package="DIP (Dual Inline) [THT]"]
  CLOCK = female pin header, 2 pins [form="♀ (female)"]
  R30 = Resistor [tolerance=±5% resistance=1k package=THT]
  R31 = Resistor [tolerance=±5% resistance=1k package=THT]
  R32 = Resistor [tolerance=±5% resistance=1k package=THT]
  R33 = Resistor [tolerance=±5% resistance=1k package=THT]
  R34 = Resistor [tolerance=±5% resistance=1k package=THT]
  R35 = Resistor [tolerance=±5% resistance=1k package=THT]
  R36 = Resistor [tolerance=±5% resistance=1k package=THT]
  R37 = Resistor [tolerance=±5% resistance=1k package=THT]
  LED21 = LED - 5mm [color="Red (633nm)" package="5 mm [THT]"]
  LED22 = LED - 5mm [color="Red (633nm)" package="5 mm [THT]"]
  LED23 = LED - 5mm [color="Red (633nm)" package="5 mm [THT]"]
  LED24 = LED - 5mm [color="Red (633nm)" package="5 mm [THT]"]
  LED25 = LED - 5mm [color="Red (633nm)" package="5 mm [THT]"]
  LED26 = LED - 5mm [color="Red (633nm)" package="5 mm [THT]"]
  LED27 = LED - 5mm [color="Red (633nm)" package="5 mm [THT]"]
  LED28 = LED - 5mm [color="Red (633nm)" package="5 mm [THT]"]
  INPUT = female pin header, 2 pins [form="♀ (female)"]
  OUTPUT = female pin header, 2 pins [form="♀ (female)"]
  BUS_2 = female pin header, 8 pins [form="♀ (female)"]
  RESULT_3 = female pin header, 8 pins [form="♀ (female)"]
  R38 = Resistor [tolerance=±5% resistance=220 package=THT]
  R39 = Resistor [tolerance=±5% resistance=220 package=THT]
  IC24 = DIP - 14 pins [chip_label=74HCT32 package="DIP (Dual Inline) [THT]"]
  IC25 = DIP - 14 pins [chip_label=74HCT32 package="DIP (Dual Inline) [THT]"]

nets:
  N1: IC11.B0, B_REGISTER.pin4
  N2: IC11.A0, BUS.pin4
  N3: IC11.S3, IC12.S3
  N4: IC11.S2, IC12.S2
  N5: IC11.S1, IC12.S1
  N6: IC11.S0, IC12.S0
  N7: IC11._CN, IC12._CN+4
  N8: IC11.M, IC12.M
  N9: IC11.F0, RESULT.pin4
  N10: IC11.F1, RESULT.pin3
  N11: IC11.F2, RESULT.pin2
  GND: IC11.GND, IC12.GND, IC13.pin1, IC13.pin2, IC13.pin7
  N12: IC11.F3, RESULT.pin1, IC16.pin12, LED18.anode
  N13: IC11.A=B, IC13.pin10
  N14: IC11._CN+4, IC13.pin4, IC13.pin5
  N15: IC11.B3, B_REGISTER.pin1
  N16: IC11.A3, BUS.pin1
  N17: IC11.B2, B_REGISTER.pin2
  N18: IC11.A2, BUS.pin2
  N19: IC11.B1, B_REGISTER.pin3
  N20: IC11.A1, BUS.pin3
  VCC: IC11.VCC, IC12.VCC, IC13.pin14
  N21: IC12.B0, B_REGISTER.pin8
  N22: IC12.A0, BUS.pin8
  N23: IC12._CN, IC17.4Y
  N24: IC12.F0, RESULT.pin8
  N25: IC12.F1, RESULT.pin7
  N26: IC12.F2, RESULT.pin6
  N27: IC12.F3, RESULT.pin5
  N28: IC12.A=B, IC13.pin9
  N29: IC12.B3, B_REGISTER.pin5
  N30: IC12.A3, BUS.pin5
  N31: IC12.B2, B_REGISTER.pin6
  N32: IC12.A2, BUS.pin6
  N33: IC12.B1, B_REGISTER.pin7
  N34: IC12.A1, BUS.pin7
  N35: IC13.pin6, IC16.pin14, LED20.anode
  N36: IC13.pin8, IC13.pin12, IC13.pin13
  N37: IC13.pin11, IC16.pin13, LED19.anode
  N38: IC16.pin1, IC16.pin2
  N39: IC16.pin3, LED2.anode
  N40: IC16.pin4, LED3.anode
  N41: IC16.pin5, LED4.anode
  N42: IC16.pin6, LED5.anode
  GND_2: IC16.pin8, R1.Pin_0, R2.Pin_0, R3.Pin_0, R4.Pin_0, IC17.1A, IC17.2A, IC17.3A, IC17.GND, R5.Pin_0, R6.Pin_0, R8.Pin_0, R9.Pin_0, R10.Pin_0, R11.Pin_0, R38.Pin_0, R39.Pin_0, IC24.1A, IC24.1B, IC24.GND, IC25.GND
  N43: IC16.pin9, IC17.6Y
  N44: IC16.pin10, IC16.pin15, IC17.6A, R13.Pin_1, R14.Pin_1, R15.Pin_1, R16.Pin_1, FLAGS_IN.pin1, FLAGS_IN.pin2
  N45: IC16.pin11, IC17.5Y, LED17.anode
  VCC_2: IC16.pin16, IC17.VCC, IC24.VCC, IC25.VCC
  N46: CARRY/BORROW_IN.pin1, CARRY/BORROW_IN.pin2, IC17.4A
  N47: LED2.cathode, R1.Pin_1
  N48: LED3.cathode, R2.Pin_1
  N49: LED4.cathode, R4.Pin_1
  N50: LED5.cathode, R3.Pin_1
  N51: IC17.5A, IC24.4Y
  N52: RESULT_2.pin1, LED10.anode, IC25.2B
  N53: RESULT_2.pin2, LED9.anode, IC25.2A
  N54: RESULT_2.pin3, LED12.anode, IC25.1B
  N55: RESULT_2.pin4, LED11.anode, IC25.1A
  N56: RESULT_2.pin5, LED14.anode, IC25.3B
  N57: RESULT_2.pin6, LED16.anode, IC25.3A
  N58: RESULT_2.pin7, LED15.anode, IC25.4A
  N59: RESULT_2.pin8, LED13.anode, IC25.4B
  N60: LED9.cathode, R6.Pin_1
  N61: LED10.cathode, R5.Pin_1
  N62: LED11.cathode, R8.Pin_1
  N63: LED12.cathode, R38.Pin_1
  N64: LED13.cathode, R11.Pin_1
  N65: LED14.cathode, R9.Pin_1
  N66: LED15.cathode, R10.Pin_1
  N67: LED16.cathode, R39.Pin_1
  N68: R13.Pin_0, LED20.cathode
  N69: R14.Pin_0, LED19.cathode
  N70: R15.Pin_0, LED18.cathode
  N71: R16.Pin_0, LED17.cathode
  N72: IC20.A1, IC21.1Q, LED22.anode
  N73: IC20.A2, IC21.2Q, LED21.anode
  N74: IC20.A3, IC21.3Q, LED24.anode
  N75: IC20.A4, IC21.4Q, LED23.anode
  N76: IC20.A5, IC21.5Q, LED26.anode
  N77: IC20.A6, IC21.6Q, LED28.anode
  N78: IC20.A7, IC21.7Q, LED27.anode
  N79: IC20.A8, IC21.8Q, LED25.anode
  GND_3: IC20.GND, IC21.GND, IC22.2A, IC22.3A, IC22.GND
  N80: IC20.B8, BUS_2.pin8
  N81: IC20.B7, BUS_2.pin7
  N82: IC20.B6, BUS_2.pin6
  N83: IC20.B5, BUS_2.pin5
  N84: IC20.B4, BUS_2.pin4
  N85: IC20.B3, BUS_2.pin3
  N86: IC20.B2, BUS_2.pin2
  N87: IC20.B1, BUS_2.pin1
  N88: IC20._OE, IC22.4Y
  VCC_3: IC20.VCC, IC21.VCC, IC22.VCC
  N89: IC21._CLKEN, IC22.1Y
  N90: IC21.1D, RESULT_3.pin1
  N91: IC21.2D, RESULT_3.pin2
  N92: IC21.3D, RESULT_3.pin3
  N93: IC21.4D, RESULT_3.pin4
  N94: IC21.CLK, CLOCK.pin1, CLOCK.pin2
  N95: IC21.5D, RESULT_3.pin5
  N96: IC21.6D, RESULT_3.pin6
  N97: IC21.7D, RESULT_3.pin7
  N98: IC21.8D, RESULT_3.pin8
  N99: IC22.1A, INPUT.pin1, INPUT.pin2
  N100: IC22.4A, OUTPUT.pin1, OUTPUT.pin2
  N101: IC22.5A, IC22.6A, R30.Pin_1, R31.Pin_1, R32.Pin_1, R33.Pin_1, R34.Pin_1, R35.Pin_1, R36.Pin_1, R37.Pin_1
  N102: R30.Pin_0, LED27.cathode
  N103: R31.Pin_0, LED26.cathode
  N104: R32.Pin_0, LED23.cathode
  N105: R33.Pin_0, LED24.cathode
  N106: R34.Pin_0, LED25.cathode
  N107: R35.Pin_0, LED28.cathode
  N108: R36.Pin_0, LED22.cathode
  N109: R37.Pin_0, LED21.cathode
  N110: IC24.2A, IC25.2Y
  N111: IC24.2B, IC25.1Y
  N112: IC24.2Y, IC24.4A
  N113: IC24.3Y, IC24.4B
  N114: IC24.3A, IC25.4Y
  N115: IC24.3B, IC25.3Y

custom parts:
  DIP - 24 pins: 4-bit ALU
  DIP - 14 pins: Hex Inverter
  74HCT245: Octal Tri state buffer
  74HCT377: Octal D-Type flip flops with clock enable 8 bit register
  DIP - 14 pins: Quad OR gate
