# Fritzing sketch clock (saved by Fritzing 0.9.3b)
breadboards: 1

parts:
  U2 = 555 Timer [package="DIP8 [THT]"]
  R7 = Resistor [tolerance=±5% resistance=220 package=THT]
  R8 = Resistor [tolerance=±5% resistance=220 package=THT]
  C6 = Electrolytic Capacitor [capacitance=1µF package="100 mil [THT, electrolytic]"]
  C7 = Ceramic Capacitor [capacitance=100nF package="100 mil [THT, multilayer]"]
  R9 = Rotary Potentiometer (Small) [maximum_resistance=100kΩ package=THT]
  R10 = Resistor [tolerance=±5% resistance=220 package=THT]
  C8 = Ceramic Capacitor [capacitance=100nF package="100 mil [THT, multilayer]"]
  R11 = Resistor [tolerance=±5% resistance=220 package=THT]
  C9 = Ceramic Capacitor [capacitance=100nF package="100 mil [THT, multilayer]"]
  IC11 = DIP - 14 pins [chip_label=74HCT14 package="DIP (Dual Inline) [THT]"]
  IC12 = DIP - 14 pins [chip_label=74HCT00 package="DIP (Dual Inline) [THT]"]
  R12 = Resistor [tolerance=±5% resistance=220 package=THT]
  C10 = Ceramic Capacitor [capacitance=100nF package="100 mil [THT, multilayer]"]
  IC13 = IC, DIP package, 14 pins [chip_label=74HCT02]
  IC14 = DIP - 14 pins [chip_label=74HCT00 package="DIP (Dual Inline) [THT]"]
  IC16 = DIP - 16 pins [chip_label=74HCT109 package="DIP (Dual Inline) [THT]"]
  IC17 = DIP - 16 pins [chip_label=74HCT109 package="DIP (Dual Inline) [THT]"]
  LED1 = LED - 5mm [color="Blue (470nm)" package="5 mm [THT]"]
  LED2 = LED - 5mm [color="Blue (470nm)" package="5 mm [THT]"]
  R13 = Resistor [tolerance=±5% resistance=220 package=THT]
  R14 = Resistor [tolerance=±5% resistance=220 package=THT]
  C11 = Ceramic Capacitor [capacitance=100nF package="100 mil [THT, multilayer]"]
  C12 = Ceramic Capacitor [capacitance=100nF package="100 mil [THT, multilayer]"]

nets:
  GND: U2.Ground, R7.Pin_1, C6.-, C7.0, C8.1, C9.0, IC11.GND, IC12.2A, IC12.2B, IC12.GND, C10.1, IC13.pin7, IC14.1A, IC14.1B, IC14.GND, IC16._1K, IC16.GND, IC16.2CP, IC16._2K, IC17._1K, IC17.GND, IC17._2K, R13.Pin_0, C11.0, C12.1
  N1: U2.Trigger, U2.Threshold, C6.+, R9.leg1
  N2: U2.Output, IC16.1CP
  VCC: U2.Reset, U2.Vcc_Supply_Voltage, IC11.VCC, IC12.VCC, IC13.pin14, IC14.VCC, IC16._1R, IC16.1J, IC16._1S, IC16._2S, IC16.2J, IC16._2R, IC16.VCC, IC17.1J, IC17._1S, IC17._2S, IC17.2J, IC17.VCC, C11.1, C12.0
  N3: U2.Control_Voltage, C7.1
  N4: U2.Discharge, R7.Pin_0, R8.Pin_0
  N5: R8.Pin_1, R9.wiper
  N6: R10.Pin_0, C8.0, IC11.3A
  N7: R11.Pin_1, C9.1, IC11.6A
  N8: IC11.1A, R12.Pin_0, C10.0
  N9: IC11.1Y, IC11.2A
  N10: IC11.2Y, IC13.pin3, IC13.pin5
  N11: IC11.3Y, IC11.4A, IC12.1A
  N12: IC11.4Y, IC12.4A
  N13: IC11.5Y, IC12.4B
  N14: IC11.5A, IC11.6Y
  N15: IC12.1B, IC16.1Q
  N16: IC12.1Y, IC12.3A
  N17: IC12.3Y, IC13.pin11, IC13.pin12, IC14.4A
  N18: IC12.3B, IC12.4Y
  N19: IC13.pin1, IC17._1R, IC17._2R
  N20: IC13.pin4, IC13.pin8, IC14.4B
  N21: IC13.pin6, IC13.pin10
  N22: IC13.pin9, IC13.pin13
  N23: IC14.2A, IC14.2B, IC14.3Y, IC17.2CP
  N24: IC14.2Y, IC17.1CP
  N25: IC14.3B, IC14.3A, IC14.4Y
  N26: IC17.1Q, LED2.anode
  N27: IC17.2Q, LED1.anode
  N28: LED1.cathode, R13.Pin_1
  N29: LED2.cathode, R14.Pin_0

notes:
  halt
  auto/manual
  manual_clock_input
  reset
  (driver clock)
  (debounced manual_clock_input)
  (debounced reset)
  (debounced auto/manual)
  data_clock
  control_clock

custom parts:
  DIP - 14 pins: Hex Schmitt trigger inverters
  DIP - 14 pins: Quad NAND
  DIP - 16 pins: Dual JK flip flop with set and reset, positive edge trigger
