# Fritzing sketch control_unit (saved by Fritzing 0.9.3b)
breadboards: 5

parts:
  IC1 = DIP - 28 pins [chip_label=AT28C256 package="DIP (Dual Inline) [THT]"]
  J1 = female pin header, 7 pins [form="♀ (female)"]
  J2 = female pin header, 8 pins [form="♀ (female)"]
  J3 = female pin header, 7 pins [form="♀ (female)"]
  IC2 = DIP - 28 pins [chip_label=AT28C256 package="DIP (Dual Inline) [THT]"]
  J4 = female pin header, 8 pins [form="♀ (female)"]
  IC7 = DIP - 16 pins [chip_label=74HCT138 package="DIP (Dual Inline) [THT]"]
  LED16 = LED - 5mm [color="Green (555nm)" package="5 mm [THT]"]
  J7 = female pin header, 8 pins [form="♀ (female)"]
  J8 = female pin header, 4 pins [form="♀ (female)"]
  J13 = female pin header, 8 pins [form="♀ (female)"]
  J14 = female pin header, 8 pins [form="♀ (female)"]
  J15 = female pin header, 8 pins [form="♀ (female)"]
  R1 = Resistor [tolerance=±5% resistance=220 package=THT]
  R2 = Resistor [tolerance=±5% resistance=220 package=THT]
  R4 = Resistor [tolerance=±5% resistance=220 package=THT]
  R5 = Resistor [tolerance=±5% resistance=220 package=THT]
  R6 = Resistor [tolerance=±5% resistance=220 package=THT]
  R7 = Resistor [tolerance=±5% resistance=220 package=THT]
  R10 = Resistor [tolerance=±5% resistance=220 package=THT]
  R12 = Resistor [tolerance=±5% resistance=220 package=THT]
  R13 = Resistor [tolerance=±5% resistance=220 package=THT]
  R15 = Resistor [tolerance=±5% resistance=220 package=THT]
  R16 = Resistor [tolerance=±5% resistance=220 package=THT]
  R17 = Resistor [tolerance=±5% resistance=220 package=THT]
  R19 = Resistor [tolerance=±5% resistance=220 package=THT]
  R22 = Resistor [tolerance=±5% resistance=220 package=THT]
  R23 = Resistor [tolerance=±5% resistance=220 package=THT]
  R24 = Resistor [tolerance=±5% resistance=220 package=THT]
  R25 = Resistor [tolerance=±5% resistance=220 package=THT]
  R26 = Resistor [tolerance=±5% resistance=220 package=THT]
  R27 = Resistor [tolerance=±5% resistance=220 package=THT]
  R29 = Resistor [tolerance=±5% resistance=220 package=THT]
  J16 = female pin header, 6 pins [form="♀ (female)"]
  IC10 = 74HCT377 [chip_label=74HCT377 package="DIP (Dual Inline) [THT]"]
  IC11 = DIP - 16 pins [chip_label=74HCT173 package="DIP (Dual Inline) [THT]"]
  IC12 = DIP - 14 pins [chip_label=74HCT04 package="DIP (Dual Inline) [THT]"]
  IC13 = DIP - 16 pins [chip_label=74HCT161 package="DIP (Dual Inline) [THT]"]
  LED59 = LED - 5mm [color="Blue (430nm)" package="5 mm [THT]"]
  LED60 = LED - 5mm [color="Blue (430nm)" package="5 mm [THT]"]
  LED61 = LED - 5mm [color="Blue (430nm)" package="5 mm [THT]"]
  MASTER_RESET = female pin header, 2 pins [form="♀ (female)"]
  C/U_TIMER_RESET3 = female pin header, 2 pins [form="♀ (female)"]
  J17 = female pin header, 8 pins [form="♀ (female)"]
  J18 = female pin header, 8 pins [form="♀ (female)"]
  C/U_TIMER_RESET4 = female pin header, 2 pins [form="♀ (female)"]
  J23 = female pin header, 3 pins [form="♀ (female)"]
  C1 = Ceramic Capacitor [capacitance=100nF package="100 mil [THT, multilayer]"]
  C2 = Ceramic Capacitor [capacitance=100nF package="100 mil [THT, multilayer]"]
  J24 = female pin header, 3 pins [form="♀ (female)"]
  R33 = Resistor [tolerance=±5% resistance=220 package=THT]
  R34 = Resistor [tolerance=±5% resistance=220 package=THT]
  R35 = Resistor [tolerance=±5% resistance=220 package=THT]
  R36 = Resistor [tolerance=±5% resistance=220 package=THT]
  R37 = Resistor [tolerance=±5% resistance=220 package=THT]
  R38 = Resistor [tolerance=±5% resistance=220 package=THT]
  R39 = Resistor [tolerance=±5% resistance=220 package=THT]
  R40 = Resistor [tolerance=±5% resistance=220 package=THT]
  R41 = Resistor [tolerance=±5% resistance=220 package=THT]
  R42 = Resistor [tolerance=±5% resistance=220 package=THT]
  R43 = Resistor [tolerance=±5% resistance=220 package=THT]
  R44 = Resistor [tolerance=±5% resistance=220 package=THT]
  R45 = Resistor [tolerance=±5% resistance=220 package=THT]
  R46 = Resistor [tolerance=±5% resistance=220 package=THT]
  R47 = Resistor [tolerance=±5% resistance=220 package=THT]
  R48 = Resistor [tolerance=±5% resistance=220 package=THT]
  R49 = Resistor [tolerance=±5% resistance=220 package=THT]
  R51 = Resistor [tolerance=±5% resistance=220 package=THT]
  R52 = Resistor [tolerance=±5% resistance=220 package=THT]
  R53 = Resistor [tolerance=±5% resistance=220 package=THT]
  J28 = female pin header, 4 pins [form="♀ (female)"]
  J29 = female pin header, 4 pins [form="♀ (female)"]
  C3 = Ceramic Capacitor [capacitance=100nF package="100 mil [THT, multilayer]"]
  C4 = Ceramic Capacitor [capacitance=100nF package="100 mil [THT, multilayer]"]
  J30 = female pin header, 8 pins [form="♀ (female)"]
  J31 = female pin header, 8 pins [form="♀ (female)"]
  C5 = Ceramic Capacitor [capacitance=100nF package="100 mil [THT, multilayer]"]
  C6 = Ceramic Capacitor [capacitance=100nF package="100 mil [THT, multilayer]"]
  IC14 = DIP - 28 pins [chip_label=AT28C256 package="DIP (Dual Inline) [THT]"]
  J32 = female pin header, 7 pins [form="♀ (female)"]
  J33 = female pin header, 8 pins [form="♀ (female)"]
  J34 = female pin header, 7 pins [form="♀ (female)"]
  J35 = female pin header, 8 pins [form="♀ (female)"]
  IC15 = DIP - 28 pins [chip_label=AT28C256 package="DIP (Dual Inline) [THT]"]
  C7 = Ceramic Capacitor [capacitance=100nF package="100 mil [THT, multilayer]"]
  C8 = Ceramic Capacitor [capacitance=100nF package="100 mil [THT, multilayer]"]
  J36 = female pin header, 8 pins [form="♀ (female)"]
  J37 = female pin header, 8 pins [form="♀ (female)"]
  C9 = Ceramic Capacitor [capacitance=100nF package="100 mil [THT, multilayer]"]  # not connected
  R54 = Resistor [tolerance=±5% resistance=220 package=THT]
  R55 = Resistor [tolerance=±5% resistance=220 package=THT]
  R56 = Resistor [tolerance=±5% resistance=220 package=THT]
  J38 = female pin header, 8 pins [form="♀ (female)"]
  J39 = female pin header, 8 pins [form="♀ (female)"]
  J40 = female pin header, 7 pins [form="♀ (female)"]
  J41 = female pin header, 7 pins [form="♀ (female)"]
  LED69 = LED - 5mm [color="Green (555nm)" package="5 mm [THT]"]
  LED70 = LED - 5mm [color="Green (555nm)" package="5 mm [THT]"]
  LED71 = LED - 5mm [color="Green (555nm)" package="5 mm [THT]"]
  LED72 = LED - 5mm [color="Blue (430nm)" package="5 mm [THT]"]
  LED73 = LED - 5mm [color="Blue (430nm)" package="5 mm [THT]"]
  LED74 = LED - 5mm [color="Blue (430nm)" package="5 mm [THT]"]
  LED75 = LED - 5mm [color="Blue (430nm)" package="5 mm [THT]"]
  LED76 = LED - 5mm [color="Blue (430nm)" package="5 mm [THT]"]
  LED77 = LED - 5mm [color="Blue (430nm)" package="5 mm [THT]"]
  LED78 = LED - 5mm [color="Blue (430nm)" package="5 mm [THT]"]
  LED79 = LED - 5mm [color="Blue (430nm)" package="5 mm [THT]"]
  LED80 = LED - 5mm [color="Green (555nm)" package="5 mm [THT]"]
  LED81 = LED - 5mm [color="Green (555nm)" package="5 mm [THT]"]
  LED82 = LED - 5mm [color="Green (555nm)" package="5 mm [THT]"]
  LED83 = LED - 5mm [color="Green (555nm)" package="5 mm [THT]"]
  LED84 = LED - 5mm [color="Green (555nm)" package="5 mm [THT]"]
  LED85 = LED - 5mm [color="Green (555nm)" package="5 mm [THT]"]
  LED86 = LED - 5mm [color="Green (555nm)" package="5 mm [THT]"]
  LED87 = LED - 5mm [color="Green (555nm)" package="5 mm [THT]"]
  R57 = Resistor [tolerance=±5% resistance=220 package=THT]
  R58 = Resistor [tolerance=±5% resistance=220 package=THT]
  R59 = Resistor [tolerance=±5% resistance=220 package=THT]
  R60 = Resistor [tolerance=±5% resistance=220 package=THT]
  R61 = Resistor [tolerance=±5% resistance=220 package=THT]
  R62 = Resistor [tolerance=±5% resistance=220 package=THT]
  R63 = Resistor [tolerance=±5% resistance=220 package=THT]
  R64 = Resistor [tolerance=±5% resistance=220 package=THT]
  R65 = Resistor [tolerance=±5% resistance=220 package=THT]
  R66 = Resistor [tolerance=±5% resistance=220 package=THT]
  LED88 = LED - 3mm [color="Yellow (595nm)" package="3 mm [THT]"]
  LED89 = LED - 3mm [color="Yellow (595nm)" package="3 mm [THT]"]
  LED90 = LED - 3mm [color="Yellow (595nm)" package="3 mm [THT]"]
  LED91 = LED - 3mm [color="Yellow (595nm)" package="3 mm [THT]"]
  LED92 = LED - 3mm [color="Yellow (595nm)" package="3 mm [THT]"]
  LED93 = LED - 3mm [color="Yellow (595nm)" package="3 mm [THT]"]
  LED94 = LED - 3mm [color="Yellow (595nm)" package="3 mm [THT]"]
  LED95 = LED - 3mm [color="Yellow (595nm)" package="3 mm [THT]"]
  LED96 = LED - 3mm [color="Yellow (595nm)" package="3 mm [THT]"]
  LED97 = LED - 3mm [color="Yellow (595nm)" package="3 mm [THT]"]
  LED98 = LED - 3mm [color="Yellow (595nm)" package="3 mm [THT]"]
  LED99 = LED - 3mm [color="Yellow (595nm)" package="3 mm [THT]"]
  LED100 = LED - 3mm [color="Yellow (595nm)" package="3 mm [THT]"]
  LED101 = LED - 3mm [color="Yellow (595nm)" package="3 mm [THT]"]
  LED102 = LED - 3mm [color="Yellow (595nm)" package="3 mm [THT]"]
  LED103 = LED - 3mm [color="Yellow (595nm)" package="3 mm [THT]"]
  LED104 = LED - 3mm [color="Yellow (595nm)" package="3 mm [THT]"]
  LED105 = LED - 3mm [color="Yellow (595nm)" package="3 mm [THT]"]
  LED106 = LED - 3mm [color="Yellow (595nm)" package="3 mm [THT]"]
  LED107 = LED - 3mm [color="Yellow (595nm)" package="3 mm [THT]"]
  LED108 = LED - 3mm [color="Yellow (595nm)" package="3 mm [THT]"]
  LED109 = LED - 3mm [color="Yellow (595nm)" package="3 mm [THT]"]
  LED110 = LED - 3mm [color="Yellow (595nm)" package="3 mm [THT]"]
  LED111 = LED - 3mm [color="Yellow (595nm)" package="3 mm [THT]"]
  LED112 = LED - 3mm [color="Yellow (595nm)" package="3 mm [THT]"]
  LED113 = LED - 3mm [color="Yellow (595nm)" package="3 mm [THT]"]
  LED114 = LED - 3mm [color="Yellow (595nm)" package="3 mm [THT]"]
  LED115 = LED - 3mm [color="Yellow (595nm)" package="3 mm [THT]"]
  LED117 = LED - 3mm [color="Yellow (595nm)" package="3 mm [THT]"]
  LED119 = LED - 3mm [color="Yellow (595nm)" package="3 mm [THT]"]
  J27 = female pin header, 7 pins [form="♀ (female)"]
  J26 = female pin header, 8 pins [form="♀ (female)"]

nets:
  N1: IC1.A14, J1.pin1, J41.pin1
  N2: IC1.A12, J1.pin3, J41.pin3
  N3: IC1.A7, J30.pin1, J38.pin1
  N4: IC1.A6, J30.pin2, J38.pin2
  N5: IC1.A5, J30.pin3, J38.pin3
  N6: IC1.A4, J30.pin4, J38.pin4
  N7: IC1.A3, J30.pin5, J38.pin5
  N8: IC1.A2, J30.pin6, J38.pin6
  N9: IC1.A1, J30.pin7, J38.pin7
  N10: IC1.A0, J30.pin8, J38.pin8
  N11: IC1.I/O0, J2.pin8
  N12: IC1.I/O1, J2.pin7
  N13: IC1.I/O2, J2.pin6
  GND: IC1.GND, IC1._CE, IC1._OE, IC2.GND, IC2._CE, IC2._OE, C5.1, C6.0
  N14: IC1.I/O3, J2.pin5
  N15: IC1.I/O4, J2.pin4
  N16: IC1.I/O5, J2.pin3
  N17: IC1.I/O6, J2.pin2
  N18: IC1.I/O7, J2.pin1
  N19: IC1.A10, J1.pin5, J41.pin5
  N20: IC1.A11, J1.pin4, J41.pin4
  N21: IC1.A9, J1.pin6, J41.pin6
  N22: IC1.A8, J1.pin7, J41.pin7
  N23: IC1.A13, J1.pin2, J41.pin2
  VCC: IC1._WE, IC1.VCC, IC2._WE, IC2.VCC, C5.0, C6.1
  N24: J3.pin1, IC2.A14, J40.pin1
  N25: J3.pin2, IC2.A13, J40.pin2
  N26: J3.pin3, IC2.A12, J40.pin3
  N27: J3.pin4, IC2.A11, J40.pin4
  N28: J3.pin5, IC2.A10, J40.pin5
  N29: J3.pin6, IC2.A9, J40.pin6
  N30: J3.pin7, IC2.A8, J40.pin7
  N31: IC2.A7, J31.pin1, J39.pin1
  N32: IC2.A6, J31.pin2, J39.pin2
  N33: IC2.A5, J31.pin3, J39.pin3
  N34: IC2.A4, J31.pin4, J39.pin4
  N35: IC2.A3, J31.pin5, J39.pin5
  N36: IC2.A2, J31.pin6, J39.pin6
  N37: IC2.A1, J31.pin7, J39.pin7
  N38: IC2.A0, J31.pin8, J39.pin8
  N39: IC2.I/O0, J4.pin8
  N40: IC2.I/O1, J4.pin7
  N41: IC2.I/O2, J4.pin6
  N42: IC2.I/O3, J4.pin5
  N43: IC2.I/O4, J4.pin4
  N44: IC2.I/O5, J4.pin3
  N45: IC2.I/O6, J4.pin2
  N46: IC2.I/O7, J4.pin1
  N47: IC7.A, J24.pin1, J26.pin1
  N48: IC7.B, J24.pin2, J26.pin2
  N49: IC7.C, J24.pin3, J26.pin3
  N50: IC7._G2A, IC7._G2B, IC7.GND, R33.Pin_1, R34.Pin_1, R35.Pin_1, R36.Pin_1, R45.Pin_1, R46.Pin_1, R47.Pin_1, R48.Pin_1, R49.Pin_1, R51.Pin_1, R52.Pin_1, R53.Pin_1, C3.1, C4.0
  N51: IC7.G1, IC7.VCC, R37.Pin_1, R38.Pin_1, R39.Pin_1, R40.Pin_1, R41.Pin_1, R42.Pin_1, R43.Pin_1, R44.Pin_1, C3.0, C4.1
  N52: IC7.Y7, LED72.anode
  N53: IC7.Y6, LED73.anode
  N54: IC7.Y5, LED74.anode
  N55: IC7.Y4, LED75.anode
  N56: IC7.Y3, LED76.anode
  N57: IC7.Y2, LED77.anode
  N58: IC7.Y1, LED78.anode
  N59: IC7.Y0, LED79.anode
  N60: LED16.cathode, R36.Pin_0
  N61: LED16.anode, J8.pin4, J26.pin4
  N62: J7.pin1, LED82.anode, J26.pin8
  N63: J7.pin2, LED84.anode, J27.pin1
  N64: J7.pin3, LED87.anode, J27.pin2
  N65: J7.pin4, LED83.anode, J27.pin3
  N66: J7.pin5, LED80.anode, J27.pin4
  N67: J7.pin6, LED85.anode, J27.pin5
  N68: J7.pin7, LED81.anode, J27.pin6
  N69: J7.pin8, LED86.anode, J27.pin7
  N70: J8.pin1, LED71.anode, J26.pin7
  N71: J8.pin2, LED70.anode, J26.pin6
  N72: J8.pin3, LED69.anode, J26.pin5
  N73: J13.pin1, LED93.anode
  N74: J13.pin2, LED94.anode
  N75: J13.pin3, LED95.anode
  N76: J13.pin4, LED92.anode
  N77: J13.pin5, LED91.anode
  N78: J13.pin6, LED90.anode
  N79: J13.pin7, LED89.anode
  N80: J13.pin8, LED88.anode
  N81: J14.pin1, LED110.anode
  N82: J14.pin2, LED108.anode
  N83: J14.pin3, LED105.anode
  N84: J14.pin4, LED107.anode
  N85: J14.pin5, LED106.anode
  N86: J14.pin6, LED104.anode
  N87: J14.pin7, LED111.anode
  N88: J14.pin8, LED109.anode
  N89: J15.pin1, LED102.anode
  N90: J15.pin2, LED97.anode
  N91: J15.pin3, LED101.anode
  N92: J15.pin4, LED103.anode
  N93: J15.pin5, LED98.anode
  N94: J15.pin6, LED100.anode
  N95: J15.pin7, LED99.anode
  N96: J15.pin8, LED96.anode
  N97: R1.Pin_0, R2.Pin_0, R4.Pin_0, R5.Pin_0, R6.Pin_0, R7.Pin_0, R10.Pin_0, R12.Pin_0, R13.Pin_0, R15.Pin_0, R16.Pin_0, R17.Pin_0, R19.Pin_0, R22.Pin_0, R23.Pin_0, R24.Pin_0, R25.Pin_0, R26.Pin_0, R27.Pin_0, R29.Pin_0, R57.Pin_0, R58.Pin_0, R59.Pin_0, R60.Pin_0, R61.Pin_0, R62.Pin_0, R63.Pin_0, R64.Pin_0, R65.Pin_0, R66.Pin_0
  N98: R1.Pin_1, LED113.cathode
  N99: R2.Pin_1, LED115.cathode
  N100: R4.Pin_1, LED112.cathode
  N101: R5.Pin_1, LED119.cathode
  N102: R6.Pin_1, LED108.cathode
  N103: R7.Pin_1, LED110.cathode
  N104: R10.Pin_1, LED107.cathode
  N105: R12.Pin_1, LED97.cathode
  N106: R13.Pin_1, LED111.cathode
  N107: R15.Pin_1, LED106.cathode
  N108: R16.Pin_1, LED109.cathode
  N109: R17.Pin_1, LED101.cathode
  N110: R19.Pin_1, LED100.cathode
  N111: R22.Pin_1, LED93.cathode
  N112: R23.Pin_1, LED98.cathode
  N113: R24.Pin_1, LED96.cathode
  N114: R25.Pin_1, LED95.cathode
  N115: R26.Pin_1, LED92.cathode
  N116: R27.Pin_1, LED90.cathode
  N117: R29.Pin_1, LED89.cathode
  N118: J16.pin1, LED113.anode
  N119: J16.pin2, LED115.anode
  N120: J16.pin3, LED114.anode
  N121: J16.pin4, LED112.anode
  N122: J16.pin5, LED119.anode
  N123: J16.pin6, LED117.anode
  GND_2: IC10._CLKEN, IC10.GND, IC11._OE, IC11._OE2, IC11.GND, IC11._E1, IC11._E2, IC11.MR, IC12.2A, IC12.3A, IC12.GND, IC12.4A, IC12.5A, IC13.P0, IC13.P1, IC13.P2, IC13.P3, IC13.GND, C1.0, C2.1, R54.Pin_1, R55.Pin_1, R56.Pin_1
  N124: IC10.1Q, J18.pin8
  N125: IC10.1D, J17.pin8
  N126: IC10.2D, J17.pin7
  N127: IC10.2Q, J18.pin7
  N128: IC10.3Q, J18.pin6
  N129: IC10.3D, J17.pin6
  N130: IC10.4D, J17.pin5
  N131: IC10.4Q, J18.pin5
  N132: IC10.CLK, IC11.CP, IC13.CP, C/U_TIMER_RESET4.pin1, C/U_TIMER_RESET4.pin2
  N133: IC10.5Q, J18.pin4
  N134: IC10.5D, J17.pin4
  N135: IC10.6D, J17.pin3
  N136: IC10.6Q, J18.pin3
  N137: IC10.7Q, J18.pin2
  N138: IC10.7D, J17.pin2
  N139: IC10.8D, J17.pin1
  N140: IC10.8Q, J18.pin1
  VCC_2: IC10.VCC, IC11.VCC, IC12.VCC, IC13.PE, IC13.TE, IC13.VCC, C1.1, C2.0
  N141: IC11.Q0, J28.pin1
  N142: IC11.Q1, J28.pin2
  N143: IC11.Q2, J28.pin3
  N144: IC11.Q3, J28.pin4
  N145: IC11.D3, J29.pin4
  N146: IC11.D2, J29.pin3
  N147: IC11.D1, J29.pin2
  N148: IC11.D0, J29.pin1
  N149: IC12.1A, MASTER_RESET.pin1, MASTER_RESET.pin2
  N150: IC12.1Y, IC13._MR
  N151: IC12.6Y, IC13._SPE
  N152: IC12.6A, C/U_TIMER_RESET3.pin1, C/U_TIMER_RESET3.pin2
  N153: IC13.Q2, LED59.anode, J23.pin1
  N154: IC13.Q1, LED60.anode, J23.pin2
  N155: IC13.Q0, LED61.anode, J23.pin3
  N156: LED59.cathode, R56.Pin_0
  N157: LED60.cathode, R55.Pin_0
  N158: LED61.cathode, R54.Pin_0
  N159: R33.Pin_0, LED71.cathode
  N160: R34.Pin_0, LED70.cathode
  N161: R35.Pin_0, LED69.cathode
  N162: R37.Pin_0, LED76.cathode
  N163: R38.Pin_0, LED78.cathode
  N164: R39.Pin_0, LED77.cathode
  N165: R40.Pin_0, LED79.cathode
  N166: R41.Pin_0, LED73.cathode
  N167: R42.Pin_0, LED75.cathode
  N168: R43.Pin_0, LED72.cathode
  N169: R44.Pin_0, LED74.cathode
  N170: R45.Pin_0, LED83.cathode
  N171: R46.Pin_0, LED84.cathode
  N172: R47.Pin_0, LED87.cathode
  N173: R48.Pin_0, LED82.cathode
  N174: R49.Pin_0, LED86.cathode
  N175: R51.Pin_0, LED81.cathode
  N176: R52.Pin_0, LED80.cathode
  N177: R53.Pin_0, LED85.cathode
  N178: IC14.A14, J32.pin1
  N179: IC14.A12, J32.pin3
  N180: IC14.A7, J37.pin1
  N181: IC14.A6, J37.pin2
  N182: IC14.A5, J37.pin3
  N183: IC14.A4, J37.pin4
  N184: IC14.A3, J37.pin5
  N185: IC14.A2, J37.pin6
  N186: IC14.A1, J37.pin7
  N187: IC14.A0, J37.pin8
  N188: IC14.I/O0, J35.pin8
  N189: IC14.I/O1, J35.pin7
  N190: IC14.I/O2, J35.pin6
  GND_3: IC14.GND, IC14._CE, IC14._OE, IC15.GND, IC15._CE, IC15._OE, C7.0, C8.1
  N191: IC14.I/O3, J35.pin5
  N192: IC14.I/O4, J35.pin4
  N193: IC14.I/O5, J35.pin3
  N194: IC14.I/O6, J35.pin2
  N195: IC14.I/O7, J35.pin1
  N196: IC14.A10, J32.pin5
  N197: IC14.A11, J32.pin4
  N198: IC14.A9, J32.pin6
  N199: IC14.A8, J32.pin7
  N200: IC14.A13, J32.pin2
  VCC_3: IC14._WE, IC14.VCC, IC15._WE, IC15.VCC, C7.1, C8.0
  N201: J33.pin1, IC15.I/O7
  N202: J33.pin2, IC15.I/O6
  N203: J33.pin3, IC15.I/O5
  N204: J33.pin4, IC15.I/O4
  N205: J33.pin5, IC15.I/O3
  N206: J33.pin6, IC15.I/O2
  N207: J33.pin7, IC15.I/O1
  N208: J33.pin8, IC15.I/O0
  N209: J34.pin1, IC15.A14
  N210: J34.pin2, IC15.A13
  N211: J34.pin3, IC15.A12
  N212: J34.pin4, IC15.A11
  N213: J34.pin5, IC15.A10
  N214: J34.pin6, IC15.A9
  N215: J34.pin7, IC15.A8
  N216: IC15.A7, J36.pin1
  N217: IC15.A6, J36.pin2
  N218: IC15.A5, J36.pin3
  N219: IC15.A4, J36.pin4
  N220: IC15.A3, J36.pin5
  N221: IC15.A2, J36.pin6
  N222: IC15.A1, J36.pin7
  N223: IC15.A0, J36.pin8
  N224: R57.Pin_1, LED114.cathode
  N225: R58.Pin_1, LED117.cathode
  N226: R59.Pin_1, LED105.cathode
  N227: R60.Pin_1, LED102.cathode
  N228: R61.Pin_1, LED104.cathode
  N229: R62.Pin_1, LED103.cathode
  N230: R63.Pin_1, LED94.cathode
  N231: R64.Pin_1, LED99.cathode
  N232: R65.Pin_1, LED91.cathode
  N233: R66.Pin_1, LED88.cathode

notes:
  step_reset
  instruction_byte
  mirror_instruction_byte
  control_clock
  master_reset
  microcode_step (210)
  microcode_step (012)
  mirror_instruction_byte (0-6)
  mirror_flags (ECNZ)
  flags (ECNZ)
  control_signal_slice_2
  control_signal_slice_3
  control_signal_slice_0
  control_signal_slice_1
  mc-step-012_mirror-flags-ZNCE_mirror-instr-byte7
  mirror-instr-byte7_mirror-flags-ENCZ_mc-step-210

custom parts:
  DIP - 28 pins: 256kbit EEPROM
  DIP - 16 pins: 3 to 8 decoder
  74HCT377: Octal D-Type flip flops with clock enable 8 bit register
  DIP - 16 pins: 4 bit register
  DIP - 14 pins: Hex Inverter
  DIP - 16 pins: 4 bit synchronous counter with load and asynchronous clear
