# Fritzing sketch decimal_display (saved by Fritzing 0.9.3b)
breadboards: 1

parts:
  IC1 = DIP - 28 pins [chip_label=AT28C256 package="DIP (Dual Inline) [THT]"]  # not connected
  U1 = 555 Timer [package="DIP8 [THT]"]  # not connected
  IC2 = DIP - 16 pins [chip_label=74HCT109 package="DIP (Dual Inline) [THT]"]  # not connected
  7_Segment1 = 7 Segment Display
  7_Segment2 = 7 Segment Display  # not connected
  7_Segment3 = 7 Segment Display  # not connected
  7_Segment4 = 7 Segment Display  # not connected

nets:
  N1: 7_Segment1.Segment_G, 7_Segment1.Segment_F

custom parts:
  DIP - 28 pins: 256kbit EEPROM
  DIP - 16 pins: Dual JK flip flop with set and reset, positive edge trigger
