# Fritzing sketch eeprom_programmer (saved by Fritzing 0.9.3b)
breadboards: 1

parts:
  Part1 = Arduino Mega 2560 (Rev3)  # not connected
  S1 = Pushbutton [package="[THT]"]
  IC1 = DIP - 28 pins [chip_label=AT28C256 package="DIP (Dual Inline) [THT]"]  # not connected

nets:
  N1: S1.Pin_1, S1.Pin_2
  N2: S1.Pin_3, S1.Pin_4

custom parts:
  DIP - 28 pins: 256kbit EEPROM
