# Fritzing sketch ram (saved by Fritzing 0.9.3b)
breadboards: 2

parts:
  IC1 = DIP - 24 pins [chip_label=6116SA15TPG package="DIP (Dual Inline) [THT]"]
  IC2 = 74HCT245 [chip_label=74HCT245 package="DIP (Dual Inline) [THT]"]
  BUS = female pin header, 8 pins [form="♀ (female)"]
  IC3 = 74HCT245 [chip_label=74HCT245 package="DIP (Dual Inline) [THT]"]
  LED9 = LED - 5mm [color="Red (633nm)" package="5 mm [THT]"]
  LED10 = LED - 5mm [color="Red (633nm)" package="5 mm [THT]"]
  LED11 = LED - 5mm [color="Red (633nm)" package="5 mm [THT]"]
  LED12 = LED - 5mm [color="Red (633nm)" package="5 mm [THT]"]
  LED13 = LED - 5mm [color="Red (633nm)" package="5 mm [THT]"]
  LED14 = LED - 5mm [color="Red (633nm)" package="5 mm [THT]"]
  LED15 = LED - 5mm [color="Red (633nm)" package="5 mm [THT]"]
  LED16 = LED - 5mm [color="Red (633nm)" package="5 mm [THT]"]
  R22 = Resistor [tolerance=±5% resistance=1k package=THT]
  R23 = Resistor [tolerance=±5% resistance=1k package=THT]
  R24 = Resistor [tolerance=±5% resistance=1k package=THT]
  R25 = Resistor [tolerance=±5% resistance=1k package=THT]
  R26 = Resistor [tolerance=±5% resistance=1k package=THT]
  R27 = Resistor [tolerance=±5% resistance=1k package=THT]
  R28 = Resistor [tolerance=±5% resistance=1k package=THT]
  R29 = Resistor [tolerance=±5% resistance=1k package=THT]
  IC11 = DIP - 16 pins [chip_label=74HCT157 package="DIP (Dual Inline) [THT]"]
  IC12 = DIP - 14 pins [chip_label=74HCT02 package="DIP (Dual Inline) [THT]"]
  IC13 = DIP - 14 pins [chip_label=74HCT08 package="DIP (Dual Inline) [THT]"]
  IC14 = DIP - 14 pins [chip_label=74HCT14 package="DIP (Dual Inline) [THT]"]
  IC15 = DIP - 14 pins [chip_label=74HCT32 package="DIP (Dual Inline) [THT]"]
  R31 = Resistor [tolerance=±5% resistance=220 package=THT]
  C2 = Ceramic Capacitor [capacitance=100nF package="100 mil [THT, multilayer]"]
  input_enable = female pin header, 2 pins [form="♀ (female)"]
  J2 = female pin header, 2 pins [form="♀ (female)"]
  J3 = female pin header, 2 pins [form="♀ (female)"]
  J4 = female pin header, 2 pins [form="♀ (female)"]
  J5 = female pin header, 2 pins [form="♀ (female)"]
  J6 = female pin header, 2 pins [form="♀ (female)"]
  J7 = female pin header, 2 pins [form="♀ (female)"]
  J8 = female pin header, 2 pins [form="♀ (female)"]
  J9 = female pin header, 2 pins [form="♀ (female)"]
  J10 = female pin header, 2 pins [form="♀ (female)"]
  J11 = female pin header, 2 pins [form="♀ (female)"]
  C3 = Ceramic Capacitor [capacitance=100nF package="100 mil [THT, multilayer]"]
  C4 = Ceramic Capacitor [capacitance=100nF package="100 mil [THT, multilayer]"]
  input_enable1 = female pin header, 2 pins [form="♀ (female)"]
  input_enable2 = female pin header, 2 pins [form="♀ (female)"]
  input_enable3 = female pin header, 2 pins [form="♀ (female)"]
  input_enable4 = female pin header, 2 pins [form="♀ (female)"]
  BUS1 = female pin header, 8 pins [form="♀ (female)"]
  BUS2 = female pin header, 8 pins [form="♀ (female)"]
  C5 = Ceramic Capacitor [capacitance=100nF package="100 mil [THT, multilayer]"]
  C6 = Ceramic Capacitor [capacitance=100nF package="100 mil [THT, multilayer]"]

nets:
  N1: IC1.A7, BUS2.pin1
  N2: IC1.A6, BUS2.pin2
  N3: IC1.A5, BUS2.pin3
  N4: IC1.A4, BUS2.pin4
  N5: IC1.A3, BUS2.pin5
  N6: IC1.A2, BUS2.pin6
  N7: IC1.A1, BUS2.pin7
  N8: IC1.A0, BUS2.pin8
  N9: IC1.I/O0, IC2.A8, IC3.A8, LED13.anode
  N10: IC1.I/O1, IC2.A7, IC3.A7, LED15.anode
  N11: IC1.I/O2, IC2.A6, IC3.A6, LED16.anode
  GND: IC1.GND, IC1._CS, IC1.A10, IC1._OE, IC1.A9, IC2.DIR, IC2.GND, IC3.GND, R22.Pin_1, R23.Pin_1, R24.Pin_1, R25.Pin_1, R27.Pin_1, R28.Pin_1, R29.Pin_1, C5.0, C6.1
  N12: IC1.I/O3, IC2.A5, IC3.A5, LED14.anode
  N13: IC1.I/O4, IC2.A4, IC3.A4, LED11.anode
  N14: IC1.I/O5, IC2.A3, IC3.A3, LED12.anode
  N15: IC1.I/O6, IC2.A2, IC3.A2, LED9.anode
  N16: IC1.I/O7, IC2.A1, IC3.A1, LED10.anode
  N17: IC1._WE, input_enable4.pin1, input_enable4.pin2
  N18: IC1.A8, input_enable3.pin1, input_enable3.pin2
  VCC: IC1.VCC, IC2.VCC, IC3.DIR, IC3.VCC, C5.1, C6.0
  N19: IC2.B8, BUS1.pin8
  N20: IC2.B7, BUS1.pin7
  N21: IC2.B6, BUS1.pin6
  N22: IC2.B5, BUS1.pin5
  N23: IC2.B4, BUS1.pin4
  N24: IC2.B3, BUS1.pin3
  N25: IC2.B2, BUS1.pin2
  N26: IC2.B1, BUS1.pin1
  N27: IC2._OE, input_enable1.pin1, input_enable1.pin2
  N28: BUS.pin1, IC3.B1
  N29: BUS.pin2, IC3.B2
  N30: BUS.pin3, IC3.B3
  N31: BUS.pin4, IC3.B4
  N32: BUS.pin5, IC3.B5
  N33: BUS.pin6, IC3.B6
  N34: BUS.pin7, IC3.B7
  N35: BUS.pin8, IC3.B8
  N36: IC3._OE, input_enable2.pin1, input_enable2.pin2
  N37: LED9.cathode, R29.Pin_0
  N38: LED10.cathode, R28.Pin_0
  N39: LED11.cathode, R24.Pin_0
  N40: LED12.cathode, R25.Pin_0
  N41: LED13.cathode, R26.Pin_0
  N42: LED14.cathode, R23.Pin_0
  N43: LED15.cathode, R22.Pin_0
  N44: LED16.cathode, R27.Pin_0
  N45: IC11._A/B, J4.pin1, J4.pin2
  N46: IC11.1A, J5.pin1, J5.pin2
  N47: IC11.1B, J6.pin1, J6.pin2
  N48: IC11.1Y, J7.pin1, J7.pin2
  N49: IC11.2A, J2.pin1, J2.pin2
  N50: IC11.2B, J3.pin1, J3.pin2
  N51: IC11.2Y, IC12.1A, IC12.1B, IC13.4B
  GND_2: IC11.GND, IC12.GND, IC13.2A, IC13.2B, IC13.GND, IC14.3A, IC14.GND, IC15.2A, IC15.2B, IC15.GND, IC15.3A, IC15.3B, C2.0, C3.0, C4.1
  N52: IC11.3Y, IC12.4A, IC12.4B
  VCC_2: IC11.3B, IC11.VCC, IC12.VCC, IC13.VCC, IC14.VCC, IC15.VCC, C3.1, C4.0
  N53: IC11.3A, input_enable.pin1, input_enable.pin2
  N54: IC12.1Y, IC12.2A
  N55: IC12.2Y, IC12.3A
  N56: IC12.2B, IC12.3Y, IC13.4A
  N57: IC12.3B, IC12.4Y
  N58: IC13.1A, IC13.1B, IC13.3A, IC13.3B, IC13.4Y
  N59: IC13.1Y, R31.Pin_1
  N60: IC13.3Y, IC14.6A
  N61: IC14.1A, R31.Pin_0, C2.1
  N62: IC14.1Y, IC15.1A, IC15.1B, IC15.4B
  N63: IC14.2A, J8.pin1, J8.pin2
  N64: IC14.2Y, J9.pin1, J9.pin2
  N65: IC14.4Y, IC15.4A
  N66: IC14.4A, IC14.5Y
  N67: IC14.5A, IC14.6Y
  N68: IC15.1Y, J11.pin1, J11.pin2
  N69: IC15.4Y, J10.pin1, J10.pin2

notes:
  input_enable
  output_enable
  _output_enable
  ram_chip__WE
  input_buffer__OE
  data_clock
  setup_clock
  run/setup 0/1
  control_unit_select_data_memory
  setup_select_data_memory
  select_data_memory
  data_in
  data_out
  address

custom parts:
  DIP - 24 pins: 2K SRAM (16K x 8-bit)
  74HCT245: Octal Tri state buffer
  DIP - 16 pins: Quad 2 line to one line data selectors
  DIP - 14 pins: Quad NOR
  DIP - 14 pins: Quad AND
  DIP - 14 pins: Hex Schmitt trigger inverters
  DIP - 14 pins: Quad OR gate
